# Fritzing sketch gs_incubation (saved by Fritzing 0.9.4)
breadboards: 1

parts:
  Parça1 = Arduino Leonardo (Rev3b)
  R1 = Rotary Potentiometer (Small) [maximum_resistance=100kΩ package=THT]
  WaterIn = smd LED [color="Green (570nm)" package="0603 [SMD]"]
  RoleLed = smd LED [color="Green (570nm)" package="0805 [SMD]"]
  R2 = Resistor [tolerance=±5% resistance=220 package=THT]
  R3 = Resistor [tolerance=±5% resistance=220 package=THT]
  WaterOut = smd LED [color="Red (660nm)" package="0603 [SMD]"]
  R4 = Resistor [tolerance=±5% resistance=220 package=THT]
  Devirdaim = smd LED [color="White (6500K)" package="0603 [SMD]"]
  R5 = Resistor [tolerance=±5% resistance=220 package=THT]
  Isıtıcı = smd LED [color="Yellow (595nm)" package="0603 [SMD]"]
  Alarm = smd LED [color="Red (660nm)" package="0603 [SMD]"]
  PWMLEd = smd LED [color="Red (660nm)" package="0603 [SMD]"]
  R6 = Resistor [tolerance=±5% resistance=220 package=THT]
  R7 = Resistor [tolerance=±5% resistance=220 package=THT]
  R8 = Resistor [tolerance=±5% resistance=220 package=THT]
  T1 = LM35 Temperature Sensor [package="TO92 [THT]"]

nets (from the breadboard view):
  N1: Parça1.D2/SDA, Parça1.SDA
  N2: Parça1.D3_PWM/SCL, RoleLed.cathode
  N3: Parça1.D5_PWM, WaterIn.cathode
  N4: Parça1.D6_PWM/A7, WaterOut.cathode
  N5: Parça1.5V, R1.leg1, R2.Pin_0, R3.Pin_0, T1.+Vs
  GND: Parça1.GND, R1.leg2, T1.GND
  N6: Parça1.A0, R1.wiper
  N7: Parça1.A5, T1.Vout
  N8: Parça1.D9_PWM/A9, Devirdaim.cathode
  N9: Parça1.D10_PWM/A10, Isıtıcı.cathode
  N10: Parça1.D11_PWM, Alarm.cathode
  N11: Parça1.D13_PWM, PWMLEd.cathode
  N12: WaterIn.anode, R3.Pin_1
  N13: RoleLed.anode, R2.Pin_1
  N14: WaterOut.anode, R4.Pin_1
  N15: Devirdaim.anode, R5.Pin_1
  N16: Isıtıcı.anode, R6.Pin_1
  N17: Alarm.anode, R7.Pin_1
  N18: PWMLEd.anode, R8.Pin_1
